# Fritzing sketch Mood Light (saved by Fritzing 0.9.2b)
breadboards: 1

parts:
  Composant1 = Photon
  LED3 = RGB LED - (4 legs) [package="5 mm [THT]"]
  R1 = Resistor [tolerance=±5% resistance=220 package=THT]
  R2 = Resistor [tolerance=±5% resistance=220 package=THT]
  R3 = Resistor [tolerance=±5% resistance=220 package=THT]
  LED4 = LED - 5mm [color="Infrared (850nm)" package="5 mm [THT]"]
  R4 = Resistor [tolerance=±5% resistance=220 package=THT]

nets:
  N1: Composant1.GND, R4.Pin_1
  N2: Composant1.D0, LED3.green_cathode, R2.Pin_0
  N3: Composant1.D1, LED3.blue_cathode, R3.Pin_0
  N4: Composant1.D2, LED3.red_cathode, R1.Pin_0
  N5: Composant1.D3, LED4.anode
  N6: Composant1.3V3, LED3.common_anode, R1.Pin_1, R2.Pin_1, R3.Pin_1
  N7: LED4.cathode, R4.Pin_0
